# Fritzing sketch Darkroom Timer (saved by Fritzing 0.9.3b)
circuit board: 7.5cm x 4cm
breadboards: 1

parts:
  ATmega328 = atmega328 [package=dip]
  10k = Resistor [tolerance=±5% resistance=220 package=THT]
  RESET = Pushbutton [package="[THT]"]
  16MHz = Crystal [frequency="16 Mhz" package=THT]
  C1 = Ceramic Capacitor [capacitance=100nF package="100 mil [THT, multilayer]"]
  C2 = Ceramic Capacitor [capacitance=100nF package="100 mil [THT, multilayer]"]
  7Segment = mystery part, 4 pins [chip_label=?]
  Encoder = mystery part, 5 pins [chip_label=?]
  RELAY = maluska dil miniaturrelais [part_number="DIL Mini RY" package=THT]
  D1 = Rectifier Diode [part_number=1N4001 package="300 mil [THT]"]
  2N22222 = NPN-Transistor [package="TO92 [THT]"]
  4k7 = Resistor [tolerance=±5% resistance=220 package=THT]
  DC_IN = mystery part, 2 pins [chip_label=?]
  SW2 = mystery part, 2 pins [chip_label=?]
  100uF = Electrolytic Capacitor [capacitance=1µF package="200 mil [THT, electrolytic]"]
  100uF_2 = Electrolytic Capacitor [capacitance=1µF package="200 mil [THT, electrolytic]"]
  AC_OUT = screw terminal, 2 pins
  AC_IN = screw terminal, 2 pins
  TO_P/S = screw terminal, 2 pins
  PROG = mystery part, 5 pins [chip_label=?]
  7805 = LM2931_FIXED [package=dpak]

nets:
  N1: ATmega328.RESET, 10k.Pin_1, RESET.Pin_3, RESET.Pin_4
  N2: ATmega328.D0_(RX), PROG.pin4
  N3: ATmega328.D1_(TX), PROG.pin5
  N4: ATmega328.D2, 7Segment.pin4
  N5: ATmega328.D3_(PWM), 7Segment.pin3
  N6: ATmega328.VCC, ATmega328.AREF, 10k.Pin_0, 7Segment.pin2, Encoder.pin2, RELAY.16, D1.cathode, 100uF_2.+, PROG.pin3, 7805.VOUT
  GND: ATmega328.GND, RESET.Pin_1, RESET.Pin_2, C1.1, C2.0, 7Segment.pin1, Encoder.pin1, 2N22222.E, DC_IN.pin1, SW2.pin1, 100uF.-, 100uF_2.-, PROG.pin1, 7805.GND
  N7: ATmega328.XLAT1, 16MHz.pin_0, C1.0
  N8: ATmega328.XLAT2, 16MHz.pin_1, C2.1
  N9: ATmega328.D8, Encoder.pin4
  N10: ATmega328.D9_(PWM), Encoder.pin5
  N11: ATmega328.D10_(PWM), Encoder.pin3
  N12: ATmega328.D11_(PWM), SW2.pin2
  N13: ATmega328.D12, 4k7.Pin_0
  N14: RELAY.1, D1.anode, 2N22222.C
  N15: RELAY.4, AC_IN.pin2, TO_P/S.pin2
  N16: RELAY.8, AC_OUT.pin2
  N17: RELAY.9, AC_OUT.pin1
  N18: RELAY.13, AC_IN.pin1, TO_P/S.pin1
  N19: 2N22222.B, 4k7.Pin_1
  N20: DC_IN.pin2, 100uF.+, 7805.VIN

notes:
  VCC
  GND
  DIO
  CLK
  SW
  APin
  BPin
  TX
  RX
  maglaras@gmail.com
  WARNING!
  HIGH VOLTAGE
  Dark Room Timer
